# Fritzing sketch VendControlRPI (saved by Fritzing 0.9.3b)
perfboards: 1

parts:
  J2 = female pin header, 3 pins [form="♀ (female)"]
  J1 = female pin header, 6 pins [form="♀ (female)"]
  Приемник = female pin header, 6 pins [form="♀ (female)"]
  Кресло = female pin header, 3 pins [form="♀ (female)"]
  PC817 = IC, DIP package, 4 pins [chip_label=PC817]
  Коричневый = Resistor [tolerance=±5% resistance=1k package=THT]
  R2 = Resistor [tolerance=±5% resistance=1k package=THT]
  CPC1018N = IC, DIP package, 4 pins [chip_label=CPC1018N]
  R4 = Resistor [tolerance=±5% resistance=1k package=THT]
  J3 = female pin header, 20 pins [form="♀ (female)"]
  Мама_-_вниз_смотрят = female pin header, 20 pins [form="♀ (female)"]  # not connected
  Дверь_внутренняя = female pin header, 3 pins [form="♀ (female)"]
  Дверь_денег = female pin header, 3 pins [form="♀ (female)"]
  J4 = female pin header, 2 pins [form="♀ (female)"]
  Конвертер_с_USB = female pin header, 2 pins [form="♀ (female)"]
  R5 = Resistor [tolerance=±5% resistance=1k package=THT]
  J5 = female pin header, 2 pins [form="♀ (female)"]
  Синий = Resistor [tolerance=±5% resistance=10k package=THT]
  R6 = Resistor [tolerance=±5% resistance=1k package=THT]
  PC817_2 = IC, DIP package, 4 pins [chip_label=PC817]
  Сенсор_кресла = female pin header, 2 pins [form="♀ (female)"]

nets:
  N1: J2.pin1, J1.pin4, Приемник.pin4, Кресло.pin1, Коричневый.Pin_0
  N2: J2.pin2, J1.pin2, Приемник.pin2, Кресло.pin2, J4.pin1, Конвертер_с_USB.pin1
  N3: J2.pin3, Кресло.pin3, CPC1018N.pin4
  N4: J1.pin1, Приемник.pin1, PC817.pin2
  N5: J1.pin3, Приемник.pin3
  N6: J1.pin5, Приемник.pin5
  N7: J1.pin6, Приемник.pin6
  N8: PC817.pin1, Коричневый.Pin_1
  N9: PC817.pin3, R2.Pin_0
  N10: PC817.pin4, J3.pin1
  N11: R2.Pin_1, J3.pin15
  N12: CPC1018N.pin1, R4.Pin_0
  N13: CPC1018N.pin2, J3.pin5, Синий.Pin_0
  N14: R4.Pin_1, J3.pin16
  N15: J3.pin9, Дверь_внутренняя.pin3
  N16: J3.pin10, R5.Pin_0
  N17: J3.pin17, Дверь_внутренняя.pin1
  N18: J3.pin19, Дверь_денег.pin1
  N19: J3.pin20, Дверь_внутренняя.pin2
  N20: J4.pin2, Конвертер_с_USB.pin2
  N21: R5.Pin_1, Синий.Pin_1, PC817_2.pin3
  N22: J5.pin1, R6.Pin_1, Сенсор_кресла.pin1
  N23: J5.pin2, PC817_2.pin2, Сенсор_кресла.pin2
  N24: R6.Pin_0, PC817_2.pin1
